# Fritzing sketch Printer (saved by Fritzing 0.8.7b)
circuit board: 8.46667cm x 5.64444cm
breadboards: 1

parts:
  Часть1 = Thermal Printer
  LED2 = LED - 5mm [color="Yellow (595nm)" package="5 mm [THT]"]
  LED3 = LED - 5mm [color="Green (565nm)" package="5 mm [THT]"]
  U1 = microSD Socket [package=usd-socket-pp]
  Часть2 = Arduino Uno (Rev3)
  Часть3 = Bluetooth Mate Silver
  R1 = Resistor [tolerance=±0.25% resistance=220 package=THT]
  R2 = Resistor [tolerance=±5% resistance=220 package=THT]

nets:
  GND: Часть1.GND#0, LED2.cathode, LED3.cathode, U1.GND, Часть2.GND
  5V: Часть1.VH, Часть2.5V, Часть3.VCC
  VIN: Часть1.GND#2, Часть2.VIN, Часть3.GND
  N1: Часть1.RXD, Часть2.D5_PWM
  N2: Часть1.TXD, Часть2.D6_PWM
  N3: LED2.anode, R2.Pin_1
  N4: LED3.anode, R1.Pin_1
  N5: U1.NC, Часть2.D9_PWM
  N6: U1.CS, Часть2.D10_PWM/SS
  N7: U1.DI, Часть2.D11_PWM/MOSI
  N8: U1.VCC, Часть2.D12/MISO
  N9: U1.SCK, Часть2.D13/SCK
  N10: Часть2.D8, R1.Pin_0
  N11: Часть2.D0/RX, Часть3.RX_5V
  N12: Часть2.D1/TX, Часть3.TX_5V
  N13: Часть2.D7, R2.Pin_0
